// Logisim project Сумматор.circ as structural Verilog: 1 circuit, main circuit main
module main (
  input  in_1,
  input  in_2,
  input  in_3,
  input  in_4,
  input  in_5,
  input  in_6,
  input  in_7,
  input  in_8,
  input  in_9,
  input  in_10,
  input  in_11,
  input  in_12,
  input  in_13,
  input  in_14,
  input  in_15,
  input  in_16,
  input  in_17,
  input  in_18,
  output out_19,
  output out_20,
  output out_21,
  output out_22,
  output out_23,
  output out_24,
  output P,
  output out_26,
  output out_27,
  output out_28,
  output out_29,
  output P_2,
  output out_31,
  output P_3,
  output out_33,
  output out_34,
  output out_35,
  output out_36,
  output out_37,
  output out_38,
  output out_39,
  output out_40
);

  wire _1_2_out, _1_out, _2_2_out, _2_out, _3_2_out, _3_out, _4_2_out, _4_out, _5_2_out, _5_out, _6_2_out,
       _6_out, _7_2_out, _7_out, _8_out, _9_out, _10_out, and_7_out, and_8_out, and_9_out, and_10_out,
       and_11_out, and_12_out, and_13_out, and_14_out, and_15_out, and_16_out, and_17_out, and_18_out,
       and_19_out, and_20_out, and_21_out, and_22_out, nand_1_out, nand_2_out, nand_3_out, nand_4_out,
       nand_5_out, nand_6_out, nand_7_out, nand_8_out, nand_9_out, nand_10_out, nand_11_out, nand_12_out,
       nand_13_out, nand_16_out, nand_17_out, nand_18_out, nand_19_out, nand_20_out, nand_21_out,
       nand_23_out, nand_24_out, nor_1_out, nor_2_out, nor_3_out, nor_4_out, nor_5_out, nor_6_out, nor_7_out,
       not_1_out, not_2_out, not_3_out, not_4_out, not_5_out, or_1_out, or_3_out, or_4_out, or_5_out,
       or_6_out, or_7_out, or_9_out, or_11_out, or_13_out, or_15_out, or_17_out, or_18_out, or_19_out,
       undriven, undriven_2, undriven_3, undriven_4, undriven_5, undriven_6, undriven_7;

  nand nand_1 (nand_1_out, in_1, in_2);
  nor nor_1 (nor_1_out, in_1, in_2);
  or or_1 (or_1_out, in_1, in_2);
  nand nand_2 (nand_2_out, in_1, in_2);
  nand nand_3 (nand_3_out, in_14, in_11);
  nand nand_4 (nand_4_out, in_15, in_12);
  nand nand_5 (nand_5_out, in_16, in_13);
  nand nand_6 (nand_6_out, in_1, nand_1_out);
  nand nand_7 (nand_7_out, nand_1_out, in_2);
  nor nor_2 (nor_2_out, in_1, nor_1_out);
  nor nor_3 (nor_3_out, nor_1_out, in_2);
  nand nand_8 (nand_8_out, in_14, nand_3_out);
  nand nand_9 (nand_9_out, nand_3_out, in_11);
  nand nand_10 (nand_10_out, in_15, nand_4_out);
  nand nand_11 (nand_11_out, nand_4_out, in_12);
  nand nand_12 (nand_12_out, in_16, nand_5_out);
  nand nand_13 (nand_13_out, nand_5_out, in_13);
  and and_1 (out_28, or_1_out, nand_2_out);
  and and_2 (out_33, in_14, in_11);
  nand nand_14 (out_22, nand_6_out, nand_7_out);
  and and_3 (out_23, in_1, in_2);
  or or_2 (out_26, nor_2_out, nor_3_out);
  nand nand_15 (out_31, nand_8_out, nand_9_out);
  nand nand_16 (nand_16_out, nand_10_out, nand_11_out);
  nand nand_17 (nand_17_out, nand_12_out, nand_13_out);
  and and_4 (out_40, in_16, in_13);
  and and_5 (out_36, nand_16_out, out_33);
  nand nand_18 (nand_18_out, out_33, nand_16_out);
  nand nand_19 (nand_19_out, out_33, nand_18_out);
  nand nand_20 (nand_20_out, nand_18_out, nand_16_out);
  nand nand_21 (nand_21_out, out_36, nand_17_out);
  and and_6 (out_39, nand_17_out, out_36);
  nand nand_22 (out_35, nand_19_out, nand_20_out);
  nand nand_23 (nand_23_out, out_36, nand_21_out);
  nand nand_24 (nand_24_out, nand_21_out, nand_17_out);
  nand nand_25 (out_38, nand_23_out, nand_24_out);
  and and_7 (and_7_out, in_3, in_4);
  or or_3 (or_3_out, in_3, in_4);
  and and_8 (and_8_out, in_7, in_8);
  or or_4 (or_4_out, in_7, in_8);
  and and_9 (and_9_out, in_9, in_10);
  or or_5 (or_5_out, in_9, in_10);
  and and_10 (and_10_out, in_17, in_18);
  or or_6 (or_6_out, in_17, in_18);
  and and_11 (and_11_out, or_3_out, in_5);
  and and_12 (and_12_out, or_4_out, P);
  and and_13 (and_13_out, or_5_out, P_2);
  and and_14 (and_14_out, or_6_out, P_3);
  and and_15 (and_15_out, and_7_out, in_5);
  or or_7 (or_7_out, in_5, or_3_out);
  or or_8 (P, and_11_out, and_7_out);
  and and_16 (and_16_out, and_8_out, P);
  or or_9 (or_9_out, P, or_4_out);
  or or_10 (P_2, and_12_out, and_8_out);
  and and_17 (and_17_out, and_9_out, P_2);
  or or_11 (or_11_out, P_2, or_5_out);
  or or_12 (P_3, and_13_out, and_9_out);
  and and_18 (and_18_out, and_10_out, P_3);
  or or_13 (or_13_out, P_3, or_6_out);
  or or_14 (out_37, and_14_out, and_10_out);
  not nor_4 (nor_4_out, P);  // NOR_Gate
  not nor_5 (nor_5_out, P_2);  // NOR_Gate
  not nor_6 (nor_6_out, P_3);  // NOR_Gate
  not nor_7 (nor_7_out, out_37);  // NOR_Gate
  and and_19 (and_19_out, or_7_out, nor_4_out);
  and and_20 (and_20_out, or_9_out, nor_5_out);
  and and_21 (and_21_out, or_11_out, nor_6_out);
  and and_22 (and_22_out, or_13_out, nor_7_out);
  or or_15 (or_15_out, and_15_out, and_19_out);
  or or_16 (out_27, and_16_out, and_20_out);
  or or_17 (or_17_out, and_17_out, and_21_out);
  or or_18 (or_18_out, and_18_out, and_22_out);
  and and_23 (out_21, or_15_out, in_6);
  and and_24 (out_20, out_27, in_6);
  and and_25 (out_29, or_17_out, in_6);
  and and_26 (out_34, or_18_out, in_6);
  not not_1 (not_1_out, out_21);
  not not_2 (not_2_out, out_20);
  not not_3 (not_3_out, out_29);
  not not_4 (not_4_out, out_34);
  not not_5 (not_5_out, out_37);
  and _0 (out_19, not_1_out, not_2_out, not_3_out, not_4_out, not_5_out);
  and _1 (_1_out, out_21, not_2_out, not_3_out, not_4_out, not_5_out);
  and _2 (_2_out, out_20, not_1_out, not_3_out, not_4_out, not_5_out);
  and _3 (_3_out, out_21, out_20, not_3_out, not_4_out, not_5_out);
  and _4 (_4_out, out_29, not_1_out, not_2_out, not_4_out, not_5_out);
  and _5 (_5_out, out_21, out_29, not_2_out, not_4_out, not_5_out);
  and _6 (_6_out, out_20, out_29, not_1_out, not_4_out, not_5_out);
  and _7 (_7_out, out_21, out_20, out_29, not_4_out, not_5_out);
  and _8 (_8_out, out_34, not_1_out, not_2_out, not_3_out, not_5_out);
  and _9 (_9_out, out_21, out_34, not_2_out, not_3_out, not_5_out);
  and _10 (_10_out, out_34, out_20, not_1_out, not_3_out, not_5_out);
  // AND_Gate _11 has open pins: in0=out_21, in1=out_20, in2=out_34, in3=not_2_out, in4=not_5_out, out=open
  // AND_Gate _12 has open pins: in0=out_29, in1=out_34, in2=not_1_out, in3=not_2_out, in4=not_5_out, out=open
  // AND_Gate _13 has open pins: in0=out_21, in1=out_29, in2=out_34, in3=not_2_out, in4=not_5_out, out=open
  // AND_Gate _14 has open pins: in0=out_20, in1=out_29, in2=out_34, in3=not_1_out, in4=not_5_out, out=open
  // AND_Gate _15 has open pins: in0=out_21, in1=out_20, in2=out_29, in3=out_34, in4=not_5_out, out=open
  // AND_Gate _16 has open pins: in0=out_37, in1=not_1_out, in2=not_2_out, in3=not_3_out, in4=not_4_out, out=open
  // AND_Gate _17 has open pins: in0=out_21, in1=out_37, in2=not_2_out, in3=not_3_out, in4=not_4_out, out=open
  // AND_Gate _18 has open pins: in0=out_20, in1=out_37, in2=not_1_out, in3=not_3_out, in4=not_4_out, out=open
  // AND_Gate _19 has open pins: in0=out_21, in1=out_20, in2=out_37, in3=not_3_out, in4=not_4_out, out=open
  // AND_Gate _20 has open pins: in0=out_29, in1=out_37, in2=not_1_out, in3=not_2_out, in4=not_4_out, out=open
  // AND_Gate _21 has open pins: in0=out_21, in1=out_29, in2=out_37, out=open
  // AND_Gate _22 has open pins: in0=out_20, in1=out_29, in2=out_37, in3=not_1_out, in4=not_4_out, out=open
  // AND_Gate _23 has open pins: in0=out_21, in1=out_20, in2=out_29, in3=out_37, in4=not_4_out, out=open
  // AND_Gate _24 has open pins: in0=out_34, in1=out_37, in2=not_1_out, in3=not_2_out, in4=not_3_out, out=open
  // AND_Gate _25 has open pins: in0=out_21, in1=out_34, in2=out_37, in3=not_2_out, in4=not_3_out, out=open
  // AND_Gate _26 has open pins: in0=out_20, in1=out_34, in2=out_37, in3=not_1_out, in4=not_3_out, out=open
  // AND_Gate _27 has open pins: in0=out_21, in1=out_20, in2=out_34, in3=out_37, in4=not_3_out, out=open
  // AND_Gate _28 has open pins: in0=out_29, in1=out_34, in2=out_37, in3=not_1_out, in4=not_2_out, out=open
  // AND_Gate _29 has open pins: in0=out_21, in1=out_29, in2=out_34, in3=out_37, in4=not_2_out, out=open
  // AND_Gate _30 has open pins: in0=out_20, in1=out_29, in2=out_34, in3=out_37, in4=not_1_out, out=open
  or _1_2 (_1_2_out, _2_out, _5_out, _6_out, _7_out, out_19, _8_out, _9_out);
  or _7_2 (_7_2_out, _2_out, _5_out, _6_out, _8_out, _9_out);
  or _6_2 (_6_2_out, out_19, _5_out, _6_out, _8_out, _9_out);
  or _2_2 (_2_2_out, out_19, _1_out, _2_out, _7_out, _8_out, _9_out);
  or _5_2 (_5_2_out, _2_out, _6_out, out_19, _8_out);
  or _4_2 (_4_2_out, _2_out, _5_out, _6_out, out_19, _8_out, _9_out);
  or _3_2 (_3_2_out, _1_out, _5_out, _6_out, out_19, _7_out, _8_out, _9_out);
  // OR_Gate or_19 has open pins: out=or_19_out
  _7_Segment_Display u_7_segment_display_1 (
    .g(or_19_out), .f(undriven_2), .a(undriven_4), .b(undriven_6), .e(undriven), .d(undriven_3),
    .c(undriven_5), .dp(undriven_7));
  _7_Segment_Display u_7_segment_display_2 (
    .g(_7_2_out), .f(_6_2_out), .a(_1_2_out), .b(_2_2_out), .e(_5_2_out), .d(_4_2_out), .c(_3_2_out));  // open: dp

  assign out_24 = out_20;

  // Notes on the sheet:
  //   S
  //   S
  //   S
  //   S
  //          P
endmodule
